// Logisim project control_unit.circ as structural Verilog: 8 circuits, main circuit 32bit-computer
// sw-en
module CPU (
  input  in_1,
  input  [6:0] in_2,
  input  in_3,
  input  in_4,
  input  in_5,
  output [6:0] out_6,
  output out_7,
  output out_8,
  output [31:0] out_9
);

  wire control_uint_1_i_en, control_uint_1_mem_en, control_uint_1_r_en, controlled_buffer_4_out,
       i_o_memory_1_en, j_pc_en, not_1_out, not_2_out, not_3_out, not_4_out, not_5_out, or_1_out, sw_en;
  wire [4:0] control_uint_1_r_d, control_uint_1_r_s, control_uint_1_r_t;
  wire [19:0] bit_extender_1_out, i_o_memory_1_out_11;
  wire [31:0] control_uint_1_i_type_out, control_uint_1_mem_address, control_uint_1_r_type_out,
       controlled_buffer_1_out, controlled_buffer_2_out, controlled_buffer_6_out, controlled_buffer_7_out,
       controlled_buffer_9_out, genral_registers_1_out_7, genral_registers_1_out_8, i_o_memory_1_out_9,
       program_counter_1_out, ram_1_data, register_1_q, rom_1_data;

  I_O_memory i_o_memory_1 (
    .en(i_o_memory_1_en), .address(control_uint_1_mem_address), .in_1(sw_en), .out_9(i_o_memory_1_out_9),
    .out_7(out_6), .out_6(out_8), .out_8(out_7), .in_3(in_2), .in_5(in_1), .out_11(i_o_memory_1_out_11),
    .in_2(controlled_buffer_1_out));
  assign controlled_buffer_1_out = out_7 ? controlled_buffer_7_out : 32'bz;  // Controlled_Buffer controlled_buffer_1
  RAM #(.addrWidth(20), .dataWidth(32)) ram_1 (
    .addr(i_o_memory_1_out_11), .data(ram_1_data), .sel(or_1_out), .clk(in_5), .ld(not_1_out));  // open: clr
  not not_1 (not_1_out, sw_en);
  not not_2 (not_2_out, i_o_memory_1_en);
  assign controlled_buffer_2_out = not_2_out ? ram_1_data : 32'bz;  // Controlled_Buffer controlled_buffer_2
  assign ram_1_data = not_2_out ? controlled_buffer_7_out : 32'bz;  // Controlled_Buffer controlled_buffer_3
  assign controlled_buffer_4_out = not_3_out ? in_4 : 1'bz;  // Controlled_Buffer controlled_buffer_4
  not not_3 (not_3_out, j_pc_en);
  assign controlled_buffer_2_out = i_o_memory_1_en ? i_o_memory_1_out_9 : 32'bz;  // Controlled_Buffer controlled_buffer_5
  assign controlled_buffer_6_out = not_4_out ? controlled_buffer_2_out : 32'bz;  // Controlled_Buffer controlled_buffer_6
  assign controlled_buffer_7_out = sw_en ? genral_registers_1_out_8 : 32'bz;  // Controlled_Buffer controlled_buffer_7
  not not_4 (not_4_out, sw_en);
  program_counter program_counter_1 (
    .j_type_enable(j_pc_en), .jump_adderss(out_9), .out(program_counter_1_out),
    .pc_enable(controlled_buffer_4_out), .clear(in_3), .clk(in_5));
  Genral_registers genral_registers_1 (
    .in_1(controlled_buffer_6_out), .in_2(in_4), .in_3(control_uint_1_r_d), .out_7(genral_registers_1_out_7),
    .out_8(genral_registers_1_out_8), .in_4(in_5), .in_6(control_uint_1_r_s), .in_5(control_uint_1_r_t));
  Register #(.width(32)) register_1 (.D(rom_1_data), .en(in_4), .Q(register_1_q), .clk(in_5));  // open: clr
  or or_1 (or_1_out, sw_en, control_uint_1_mem_en);
  Bit_Extender #(.in_width(32), .out_width(20)) bit_extender_1 (.in(program_counter_1_out), .out(bit_extender_1_out));
  ROM #(.addrWidth(20), .dataWidth(32)) rom_1 (.addr(bit_extender_1_out), .data(rom_1_data), .sel(in_4));
  control_uint control_uint_1 (
    .Instruction_data(register_1_q), .R_type_out(control_uint_1_r_type_out),
    .i_type_out(control_uint_1_i_type_out), .jump_address_2(out_9), .jump_enable(j_pc_en),
    .R_S(control_uint_1_r_s), .R_T(control_uint_1_r_t), .R_D(control_uint_1_r_d),
    .data_1(genral_registers_1_out_7), .in_5(genral_registers_1_out_7), .data_2(genral_registers_1_out_8),
    .rt(control_uint_1_r_d), .rs(control_uint_1_r_s), .i_en(control_uint_1_i_en), .r_en(control_uint_1_r_en),
    .mem_en(control_uint_1_mem_en), .mem_address(control_uint_1_mem_address), .sw_en(sw_en),
    .rd(control_uint_1_r_t), .in_4(genral_registers_1_out_8), .jump_address(out_9));  // open: R_type_carry, i_type_carry
  assign controlled_buffer_6_out = not_5_out ? controlled_buffer_9_out : 32'bz;  // Controlled_Buffer controlled_buffer_8
  assign controlled_buffer_9_out = control_uint_1_r_en ? control_uint_1_r_type_out : 32'bz;  // Controlled_Buffer controlled_buffer_9
  assign controlled_buffer_9_out = control_uint_1_i_en ? control_uint_1_i_type_out : 32'bz;  // Controlled_Buffer controlled_buffer_10
  not not_5 (not_5_out, or_1_out);

  // Other names for the same wires on the sheet: clk = in_5; en = in_4; jump_ad[31:0] = out_9

  // Notes on the sheet:
  //   contents of rom_1 (hex, n*v repeats v):
  //   0 20220000 c230000 20240000 24250000 28000000
endmodule

module Genral_registers (
  input  [31:0] in_1,
  input  in_2,
  input  [4:0] in_3,
  input  in_4,
  input  [4:0] in_5,
  input  [4:0] in_6,
  output [31:0] out_7,
  output [31:0] out_8
);

  wire demultiplexer_1_out0, demultiplexer_1_out1, demultiplexer_1_out2, demultiplexer_1_out3,
       demultiplexer_1_out4, demultiplexer_1_out5, demultiplexer_1_out6, demultiplexer_1_out7;
  wire [31:0] register_1_q, register_2_q, register_3_q, register_4_q, register_5_q, register_6_q,
       register_7_q, register_8_q;

  Demultiplexer #(.select(5), .enable("false")) demultiplexer_1 (
    .out0(demultiplexer_1_out0), .out1(demultiplexer_1_out1), .out2(demultiplexer_1_out2),
    .out3(demultiplexer_1_out3), .out4(demultiplexer_1_out4), .out5(demultiplexer_1_out5),
    .out6(demultiplexer_1_out6), .out7(demultiplexer_1_out7), .in(in_2), .sel(in_3));  // open: out8, out9, out10, out11, out12, out13, out14, out15, out16, out17, out18, out19, out20, out21, out22, out23, out24, out25, out26, out27, out28, out29, out30, out31
  Register #(.width(32)) register_1 (
    .D({32{1'b0}}), .en(demultiplexer_1_out0), .Q(register_1_q), .clk(in_4));  // open: clr
  Register #(.width(32)) register_2 (.D(in_1), .en(demultiplexer_1_out1), .Q(register_2_q), .clk(in_4));  // open: clr
  Register #(.width(32)) register_3 (.D(in_1), .en(demultiplexer_1_out2), .Q(register_3_q), .clk(in_4));  // open: clr
  Register #(.width(32)) register_4 (.D(in_1), .en(demultiplexer_1_out3), .Q(register_4_q), .clk(in_4));  // open: clr
  Register #(.width(32)) register_5 (.D(in_1), .en(demultiplexer_1_out4), .Q(register_5_q), .clk(in_4));  // open: clr
  Register #(.width(32)) register_6 (.D(in_1), .en(demultiplexer_1_out5), .Q(register_6_q), .clk(in_4));  // open: clr
  Register #(.width(32)) register_7 (.D(in_1), .en(demultiplexer_1_out6), .Q(register_7_q), .clk(in_4));  // open: clr
  Register #(.width(32)) register_8 (.D(in_1), .en(demultiplexer_1_out7), .Q(register_8_q), .clk(in_4));  // open: clr
  Multiplexer #(.select(5), .width(32), .enable("false")) multiplexer_1 (
    .in0(register_1_q), .in1(register_2_q), .in2(register_3_q), .in3(register_4_q), .in4(register_5_q),
    .in5(register_6_q), .in6(register_7_q), .in7(register_8_q), .out(out_7), .sel(in_6));  // open: in8, in9, in10, in11, in12, in13, in14, in15, in16, in17, in18, in19, in20, in21, in22, in23, in24, in25, in26, in27, in28, in29, in30, in31
  Multiplexer #(.select(5), .width(32), .enable("false")) multiplexer_2 (
    .in0(register_1_q), .in1(register_2_q), .in2(register_3_q), .in3(register_4_q), .in4(register_5_q),
    .in5(register_6_q), .in6(register_7_q), .in7(register_8_q), .out(out_8), .sel(in_5));  // open: in8, in9, in10, in11, in12, in13, in14, in15, in16, in17, in18, in19, in20, in21, in22, in23, in24, in25, in26, in27, in28, in29, in30, in31
endmodule

module control_uint (
  input  [31:0] data_1,
  input  [31:0] data_2,
  input  [31:0] Instruction_data,
  input  [31:0] in_4,
  input  [31:0] in_5,
  output [4:0] R_S,
  output [4:0] R_T,
  output [4:0] R_D,
  output [31:0] R_type_out,
  output R_type_carry,
  output r_en,
  output [31:0] jump_address,
  output [31:0] i_type_out,
  output [4:0] rs,
  output i_en,
  output [4:0] rt,
  output [4:0] rd,
  output i_type_carry,
  output sw_en,
  output [31:0] mem_address,
  output mem_en,
  output jump_enable,
  output [31:0] jump_address_2
);

  wire comparator_2_eq, i_type_finder_1_br_en, multiplexer_6_out, not_1_out, not_2_out, or_1_out, or_2_out;
  wire [5:0] i_type_finder_1_out;
  wire [31:0] bit_extender_1_out, controlled_buffer_2_out, controlled_buffer_4_out, multiplexer_1_out,
       multiplexer_2_out, multiplexer_3_out, n32_bit_alu_2_out_6;

  Comparator #(.width(6)) comparator_1 (.a(Instruction_data[31:26]), .b({6{1'b0}}), .eq(r_en));  // open: gt, lt
  I_type_finder i_type_finder_1 (
    .opcode(Instruction_data[31:26]), .out(i_type_finder_1_out), .out_3(i_en), .lw_enable(mem_en),
    .sw_enable(sw_en), .BR_EN(i_type_finder_1_br_en));
  Comparator #(.width(6)) comparator_2 (
    .a(Instruction_data[31:26]), .b(6'b001010), .eq(comparator_2_eq));  // open: gt, lt
  Multiplexer #(.width(32), .enable("false")) multiplexer_1 (
    .in0({32{1'b0}}), .in1(Instruction_data),
    .out({multiplexer_1_out[31:20], R_D, R_T, R_S, multiplexer_1_out[4:0]}), .sel(r_en));
  Multiplexer #(.width(32), .enable("false")) multiplexer_2 (
    .in0({32{1'b0}}), .in1(Instruction_data), .out({multiplexer_2_out[31:21], rs, multiplexer_2_out[15:0]}),
    .sel(i_en));
  Multiplexer #(.width(32), .enable("false")) multiplexer_3 (
    .in0({32{1'b0}}), .in1(Instruction_data), .out(multiplexer_3_out), .sel(comparator_2_eq));
  assign bit_extender_1_out = {{16{1'b0}}, multiplexer_2_out[15:0]};  // Bit_Extender bit_extender_1
  Demultiplexer #(.width(5), .enable("false")) demultiplexer_1 (
    .out0(rt), .out1(rd), .in(multiplexer_2_out[25:21]), .sel(or_1_out));
  or or_1 (or_1_out, i_type_finder_1_br_en, sw_en);
  assign jump_address = i_type_finder_1_br_en ? bit_extender_1_out : 32'bz;  // Controlled_Buffer controlled_buffer_1
  assign controlled_buffer_2_out = not_1_out ? bit_extender_1_out : 32'bz;  // Controlled_Buffer controlled_buffer_2
  assign jump_address_2 = {{6{1'b0}}, multiplexer_3_out[25:0]};  // Bit_Extender bit_extender_2
  assign controlled_buffer_2_out = i_type_finder_1_br_en ? in_4 : 32'bz;  // Controlled_Buffer controlled_buffer_3
  not not_1 (not_1_out, i_type_finder_1_br_en);
  _32_bit_ALU u_32_bit_alu_1 (
    .A(data_1), .B(data_2), .shift_bit(multiplexer_1_out[4:0]), .out_6(R_type_out), .carry(R_type_carry),
    .Function_bit(multiplexer_1_out[25:20]));
  _32_bit_ALU u_32_bit_alu_2 (
    .A(controlled_buffer_2_out), .B(in_5), .shift_bit({5{1'b0}}), .out_6(n32_bit_alu_2_out_6),
    .carry(i_type_carry), .Function_bit(i_type_finder_1_out));
  assign controlled_buffer_4_out = i_type_finder_1_br_en ? n32_bit_alu_2_out_6 : 32'bz;  // Controlled_Buffer controlled_buffer_4
  or or_2 (or_2_out, i_type_finder_1_br_en, mem_en);
  not not_2 (not_2_out, controlled_buffer_4_out[0]);
  Multiplexer #(.width(32), .enable("false")) multiplexer_4 (
    .in0(n32_bit_alu_2_out_6), .in1({32{1'b0}}), .out(i_type_out), .sel(or_2_out));
  Multiplexer #(.width(32), .enable("false")) multiplexer_5 (
    .in0({32{1'b0}}), .in1(n32_bit_alu_2_out_6), .out(mem_address), .sel(mem_en));
  Multiplexer #(.enable("false")) multiplexer_6 (
    .in0(1'b0), .in1(not_2_out), .out(multiplexer_6_out), .sel(i_type_finder_1_br_en));
  or or_3 (jump_enable, multiplexer_6_out, comparator_2_eq);

  // Notes on the sheet:
  //   R-type
  //   I-type
  //   J-type
endmodule

module program_counter (
  input  j_type_enable,
  input  [31:0] jump_adderss,
  input  pc_enable,
  input  clk,
  input  clear,
  output [31:0] out
);

  wire not_1_out;
  wire [31:0] adder_1_out, controlled_buffer_2_out, register_1_q;

  not not_1 (not_1_out, j_type_enable);
  assign out = j_type_enable ? jump_adderss : 32'bz;  // Controlled_Buffer controlled_buffer_1
  assign controlled_buffer_2_out = not_1_out ? adder_1_out : 32'bz;  // Controlled_Buffer controlled_buffer_2
  assign controlled_buffer_2_out = j_type_enable ? jump_adderss : 32'bz;  // Controlled_Buffer controlled_buffer_3
  Register #(.width(32)) register_1 (
    .D(controlled_buffer_2_out), .en(pc_enable), .Q(register_1_q), .clk(clk), .clr(clear));
  Adder #(.width(32)) adder_1 (.a(register_1_q), .b(32'h1), .out(adder_1_out));  // open: cin, cout
  assign out = not_1_out ? register_1_q : 32'bz;  // Controlled_Buffer controlled_buffer_4
endmodule

module _32_bit_ALU (
  input  [31:0] A,
  input  [31:0] B,
  input  [5:0] Function_bit,
  input  [4:0] shift_bit,
  output carry,
  output [31:0] out_6
);

  wire comparator_1_eq, comparator_2_gt, comparator_3_lt;
  wire [31:0] adder_1_out, and_1_out, bit_extender_1_out, bit_extender_2_out, bit_extender_3_out,
       divider_1_out, multiplexer_1_out, multiplier_1_out, nand_1_out, nor_1_out, not_1_out, or_1_out,
       shifter_1_out, undriven;

  Multiplexer #(.width(32), .enable("false")) multiplexer_1 (
    .in0(B), .in1(not_1_out), .out(multiplexer_1_out), .sel(Function_bit[0]));
  assign not_1_out = ~B;  // NOT_Gate not_1, 32 bits wide
  Adder #(.width(32)) adder_1 (.a(A), .b(multiplexer_1_out), .out(adder_1_out), .cin(Function_bit[0]), .cout(carry));
  Shifter #(.width(32)) shifter_1 (.in(A), .\dist (shift_bit), .out(shifter_1_out));
  Comparator #(.width(32), .mode("unsigned")) comparator_1 (.a(A), .b(B), .eq(comparator_1_eq));  // open: gt, lt
  assign bit_extender_1_out = {{31{1'b0}}, comparator_1_eq};  // Bit_Extender bit_extender_1
  Comparator #(.width(32), .mode("unsigned")) comparator_2 (.a(A), .b(B), .gt(comparator_2_gt));  // open: eq, lt
  assign bit_extender_2_out = {{31{1'b0}}, comparator_2_gt};  // Bit_Extender bit_extender_2
  assign bit_extender_3_out = {{31{1'b0}}, comparator_3_lt};  // Bit_Extender bit_extender_3
  Comparator #(.width(32), .mode("unsigned")) comparator_3 (.a(A), .b(B), .lt(comparator_3_lt));  // open: gt, eq
  assign and_1_out = A & B;  // AND_Gate and_1, 32 bits wide
  assign or_1_out = A | B;  // OR_Gate or_1, 32 bits wide
  Multiplier #(.width(32)) multiplier_1 (.a(A), .b(B), .out(multiplier_1_out));  // open: cin, cout
  Divider #(.width(32)) divider_1 (.a(A), .b(B), .out(divider_1_out));  // open: upper, rem
  assign nand_1_out = ~(A & B);  // NAND_Gate nand_1, 32 bits wide
  assign nor_1_out = ~(A | B);  // NOR_Gate nor_1, 32 bits wide
  Multiplexer #(.select(4), .width(32), .enable("false")) multiplexer_2 (
    .in0(adder_1_out), .in1(adder_1_out), .in2(shifter_1_out), .in3(bit_extender_1_out),
    .in4(bit_extender_2_out), .in5(bit_extender_3_out), .in6(and_1_out), .in7(or_1_out),
    .in8(multiplier_1_out), .in9(divider_1_out), .in10(undriven), .in11(nor_1_out), .in12(nor_1_out),
    .in13(nor_1_out), .in14(nor_1_out), .in15(nor_1_out), .out(out_6), .sel(Function_bit[3:0]));
endmodule

module I_type_finder (
  input  [5:0] opcode,
  output [5:0] out,
  output out_3,
  output BR_EN,
  output lw_enable,
  output sw_enable
);

  wire comparator_1_eq, comparator_2_eq, comparator_3_eq, comparator_4_eq, comparator_5_eq, comparator_6_eq,
       comparator_7_eq, comparator_8_eq, or_1_out;
  wire [5:0] controlled_buffer_2_out, multiplexer_1_out, multiplexer_2_out;

  Comparator #(.width(6)) comparator_1 (.a(opcode), .b(6'b000001), .eq(comparator_1_eq));  // open: gt, lt
  Comparator #(.width(6)) comparator_2 (.a(opcode), .b(6'b000010), .eq(comparator_2_eq));  // open: gt, lt
  Comparator #(.width(6)) comparator_3 (.a(opcode), .b(6'b000011), .eq(comparator_3_eq));  // open: gt, lt
  Comparator #(.width(6)) comparator_4 (.a(opcode), .b(6'b000100), .eq(comparator_4_eq));  // open: gt, lt
  Comparator #(.width(6)) comparator_5 (.a(opcode), .b(6'b000101), .eq(comparator_5_eq));  // open: gt, lt
  Comparator #(.width(6)) comparator_6 (.a(opcode), .b(6'b000110), .eq(comparator_6_eq));  // open: gt, lt
  Comparator #(.width(6)) comparator_7 (.a(opcode), .b(6'b000111), .eq(comparator_7_eq));  // open: gt, lt
  Comparator #(.width(6)) comparator_8 (.a(opcode), .b(6'b001000), .eq(comparator_8_eq));  // open: gt, lt
  Comparator #(.width(6)) comparator_9 (.a(opcode), .b(6'b001001), .eq(sw_enable));  // open: gt, lt
  or or_1 (or_1_out, comparator_1_eq, comparator_2_eq);
  or or_2 (BR_EN, comparator_3_eq, comparator_4_eq, comparator_5_eq, comparator_6_eq, comparator_7_eq);
  or or_3 (lw_enable, comparator_8_eq, sw_enable);
  or or_4 (out_3, or_1_out, BR_EN, lw_enable);
  Multiplexer #(.width(6), .enable("false")) multiplexer_1 (
    .in0({6{1'b0}}), .in1(6'b000001), .out(multiplexer_1_out), .sel(lw_enable));
  Multiplexer #(.width(6), .enable("false")) multiplexer_2 (
    .in0({6{1'b0}}), .in1(opcode), .out(multiplexer_2_out), .sel(or_1_out));
  assign out = BR_EN ? opcode : 6'bz;  // Controlled_Buffer controlled_buffer_1
  assign controlled_buffer_2_out = lw_enable ? multiplexer_1_out : 6'bz;  // Controlled_Buffer controlled_buffer_2
  assign controlled_buffer_2_out = or_1_out ? multiplexer_2_out : 6'bz;  // Controlled_Buffer controlled_buffer_3
  Subtractor #(.width(6)) subtractor_1 (.a(controlled_buffer_2_out), .b(6'b000001), .out(out));  // open: bin, bout

  // Notes on the sheet:
  //   add
  //   sub
  //   =
  //   >
  //   <
  //   and
  //   or
  //   Lw
  //   sw
endmodule

module I_O_memory (
  input  in_1,
  input  [31:0] in_2,
  input  [6:0] in_3,
  input  [31:0] address,
  input  in_5,
  output out_6,
  output [6:0] out_7,
  output out_8,
  output [31:0] out_9,
  output en,
  output [19:0] out_11
);

  wire comparator_1_eq, comparator_2_eq, comparator_3_eq, comparator_4_eq, demultiplexer_1_out2, not_1_out,
       not_2_out;
  wire [2:0] multiplexer_1_out, multiplexer_2_out, multiplexer_3_out, multiplexer_4_out, or_2_out;
  wire [6:0] bit_extender_2_out, multiplexer_5_out;
  wire [31:0] bit_extender_3_out, controlled_buffer_1_out;

  Comparator #(.width(32)) comparator_1 (.a(address), .b(32'hfffff0), .eq(comparator_1_eq));  // open: gt, lt
  Comparator #(.width(32)) comparator_2 (.a(address), .b(32'hfffff1), .eq(comparator_2_eq));  // open: gt, lt
  Comparator #(.width(32)) comparator_3 (.a(address), .b(32'hfffff2), .eq(comparator_3_eq));  // open: gt, lt
  Comparator #(.width(32)) comparator_4 (.a(address), .b(32'hfffff3), .eq(comparator_4_eq));  // open: gt, lt
  Multiplexer #(.width(3), .enable("false")) multiplexer_1 (
    .in0(3'b000), .in1(3'b001), .out(multiplexer_1_out), .sel(comparator_1_eq));
  Multiplexer #(.width(3), .enable("false")) multiplexer_2 (
    .in0(3'b000), .in1(3'b010), .out(multiplexer_2_out), .sel(comparator_2_eq));
  Multiplexer #(.width(3), .enable("false")) multiplexer_3 (
    .in0(3'b000), .in1(3'b011), .out(multiplexer_3_out), .sel(comparator_3_eq));
  Multiplexer #(.width(3), .enable("false")) multiplexer_4 (
    .in0(3'b000), .in1(3'b100), .out(multiplexer_4_out), .sel(comparator_4_eq));
  or or_1 (en, comparator_4_eq, comparator_3_eq, comparator_2_eq, comparator_1_eq);
  not not_1 (not_1_out, en);
  Demultiplexer #(.select(3), .enable("false")) demultiplexer_1 (
    .out1(out_6), .out2(demultiplexer_1_out2), .out3(out_8), .in(1'b1), .sel(or_2_out));  // open: out0, out4, out5, out6, out7
  assign or_2_out = multiplexer_1_out | multiplexer_2_out | multiplexer_3_out | multiplexer_4_out;  // OR_Gate or_2, 3 bits wide
  Bit_Extender #(.in_width(32), .out_width(20)) bit_extender_1 (.in(controlled_buffer_1_out), .out(out_11));
  assign controlled_buffer_1_out = not_1_out ? address : 32'bz;  // Controlled_Buffer controlled_buffer_1
  assign bit_extender_2_out = {{6{1'b0}}, in_5};  // Bit_Extender bit_extender_2
  not not_2 (not_2_out, in_1);
  Multiplexer #(.select(3), .width(7), .enable("false")) multiplexer_5 (
    .in1(in_3), .in2(bit_extender_2_out), .out(multiplexer_5_out), .sel(or_2_out));  // open: in0, in3, in4, in5, in6, in7
  assign out_7 = in_1 ? in_2[6:0] : 7'bz;  // Controlled_Buffer controlled_buffer_2
  assign bit_extender_3_out = {{25{1'b0}}, multiplexer_5_out};  // Bit_Extender bit_extender_3
  assign out_9 = not_2_out ? bit_extender_3_out : 32'bz;  // Controlled_Buffer controlled_buffer_3
endmodule

module _32bit_computer (
  input  in_1,
  input  in_2,
  input  in_3,
  input  in_4
);

  wire clock_1_out, controlled_buffer_1_out, cpu_1_out_7, cpu_1_out_8, keyboard_1_avail;
  wire [6:0] cpu_1_out_6, keyboard_1_data;

  Clock clock_1 (.out(clock_1_out));
  TTY tty_1 (.data(cpu_1_out_6), .clk(clock_1_out), .we(cpu_1_out_7), .clr(in_1));
  assign controlled_buffer_1_out = cpu_1_out_8 ? clock_1_out : 1'bz;  // Controlled_Buffer controlled_buffer_1
  Keyboard keyboard_1 (
    .clk(controlled_buffer_1_out), .re(cpu_1_out_8), .clr(in_4), .avail(keyboard_1_avail),
    .data(keyboard_1_data));
  CPU cpu_1 (
    .in_4(in_2), .in_3(in_3), .in_5(clock_1_out), .out_6(cpu_1_out_6), .out_7(cpu_1_out_7),
    .in_1(keyboard_1_avail), .in_2(keyboard_1_data), .out_8(cpu_1_out_8));  // open: out_9
endmodule
